// Digital circuit CSRs.dig as structural Verilog
module CSRs (
  input  [31:0] mepc,
  input  [31:0] mcause,
  input  [31:0] CSR_write,
  input  clock,
  input  [11:0] csr_address,
  input  write,
  input  [31:0] mtval,
  input  instr_cnt,
  input  trap,
  input  mret,
  output [31:0] CSR_read,
  output illegal_op,
  output [31:0] mtvec,
  output [31:0] mepc_read
);

  wire demultiplexer_1_out_0, demultiplexer_1_out_1, demultiplexer_1_out_2, demultiplexer_1_out_3,
       demultiplexer_1_out_4, demultiplexer_1_out_8, demultiplexer_1_out_9, demultiplexer_1_out_10,
       demultiplexer_1_out_11, demultiplexer_1_out_12, demultiplexer_1_out_14, demultiplexer_1_out_15,
       illegal_op_detect, mcycle__0xB00_ovf, minstret__0xB02_ovf, or_1_out, or_2_out, or_3_out;
  wire [3:0] selector;
  wire [31:0] mcause__0x342_q, mcycle__0xB00_out, mcycleh__0xB80_out, mie__0x304_q, minstret__0xB02_out,
       minstreth__0xB82_out, mip__0x344_q, mscratch__0x340_q, mstatus_regiter_1_output, mtval__0x343_q,
       multiplexer_1_out, multiplexer_2_out, multiplexer_3_out;

  csrs_addresses_arbiter csrs_addresses_arbiter_1 (
    .csr_address(csr_address), .illegal_op_detected(illegal_op_detect), .mux_selector(selector));
  Demultiplexer #(.Selector_Bits(4)) demultiplexer_1 (
    .sel(selector), .in(write), .out_0(demultiplexer_1_out_0), .out_1(demultiplexer_1_out_1),
    .out_2(demultiplexer_1_out_2), .out_3(demultiplexer_1_out_3), .out_4(demultiplexer_1_out_4),
    .out_8(demultiplexer_1_out_8), .out_9(demultiplexer_1_out_9), .out_10(demultiplexer_1_out_10),
    .out_11(demultiplexer_1_out_11), .out_12(demultiplexer_1_out_12), .out_14(demultiplexer_1_out_14),
    .out_15(demultiplexer_1_out_15));  // open: out_5, out_6, out_7, out_13
  or or_1 (or_1_out, trap, demultiplexer_1_out_1);
  or or_2 (or_2_out, trap, demultiplexer_1_out_2);
  or or_3 (or_3_out, trap, demultiplexer_1_out_3);
  mstatus_regiter mstatus_regiter_1 (
    .\output (mstatus_regiter_1_output), .\input (CSR_write), .clock(clock), .write(demultiplexer_1_out_12),
    .trap_firing(trap), .mret(mret));
  Multiplexer #(.Bits(32)) multiplexer_1 (.sel(trap), .in_0(CSR_write), .in_1(mepc), .out(multiplexer_1_out));
  Multiplexer #(.Bits(32)) multiplexer_2 (.sel(trap), .in_0(CSR_write), .in_1(mcause), .out(multiplexer_2_out));
  Multiplexer #(.Bits(32)) multiplexer_3 (.sel(trap), .in_0(CSR_write), .in_1(mtval), .out(multiplexer_3_out));
  Register #(.Bits(32)) mie__0x304 (.D(CSR_write), .C(clock), .en(demultiplexer_1_out_14), .Q(mie__0x304_q));
  Register #(.Bits(32)) mtvec__0x305 (.D(CSR_write), .C(clock), .en(demultiplexer_1_out_15), .Q(mtvec));
  Register #(.Bits(32)) mscratch__0x340 (.D(CSR_write), .C(clock), .en(demultiplexer_1_out_0), .Q(mscratch__0x340_q));
  Register #(.Bits(32)) mepc__0x341 (.D(multiplexer_1_out), .C(clock), .en(or_1_out), .Q(mepc_read));
  Register #(.Bits(32)) mcause__0x342 (.D(multiplexer_2_out), .C(clock), .en(or_2_out), .Q(mcause__0x342_q));
  Register #(.Bits(32)) mtval__0x343 (.D(multiplexer_3_out), .C(clock), .en(or_3_out), .Q(mtval__0x343_q));
  Register #(.Bits(32)) mip__0x344 (.D(CSR_write), .C(clock), .en(demultiplexer_1_out_4), .Q(mip__0x344_q));
  CounterPreset #(.Bits(32)) mcycle__0xB00 (
    .en(1'b1), .C(clock), .dir(1'b0), .in(CSR_write), .ld(demultiplexer_1_out_8), .clr(1'b0),
    .out(mcycle__0xB00_out), .ovf(mcycle__0xB00_ovf));
  CounterPreset #(.Bits(32)) mcycleh__0xB80 (
    .en(mcycle__0xB00_ovf), .C(clock), .dir(1'b0), .in(CSR_write), .ld(demultiplexer_1_out_9), .clr(1'b0),
    .out(mcycleh__0xB80_out));  // open: ovf
  CounterPreset #(.Bits(32)) minstret__0xB02 (
    .en(instr_cnt), .C(clock), .dir(1'b0), .in(CSR_write), .ld(demultiplexer_1_out_10), .clr(1'b0),
    .out(minstret__0xB02_out), .ovf(minstret__0xB02_ovf));
  CounterPreset #(.Bits(32)) minstreth__0xB82 (
    .en(minstret__0xB02_ovf), .C(clock), .dir(1'b0), .in(CSR_write), .ld(demultiplexer_1_out_11), .clr(1'b0),
    .out(minstreth__0xB82_out));  // open: ovf
  and and_1 (illegal_op, write, illegal_op_detect);
  Multiplexer #(.Selector_Bits(4), .Bits(32)) multiplexer_4 (
    .sel(selector), .in_0(mscratch__0x340_q), .in_1(mepc_read), .in_2(mcause__0x342_q),
    .in_3(mtval__0x343_q), .in_4(mip__0x344_q), .in_5({32{1'b0}}), .in_6({32{1'b0}}), .in_7({32{1'b0}}),
    .in_8(mcycle__0xB00_out), .in_9(mcycleh__0xB80_out), .in_10(minstret__0xB02_out),
    .in_11(minstreth__0xB82_out), .in_12(mstatus_regiter_1_output), .in_13(32'h100), .in_14(mie__0x304_q),
    .in_15(mtvec), .out(CSR_read));

  // Other names for the same wires on the sheet: clk = clock; inst_count = instr_cnt; mret_instruction = mret;
  //   trap_firing = trap

  // Notes on the sheet:
  //   CSR
  //   addresses
  //   Arbiter
  //   mvendorid (0xF11)
  //   mconfigptr (0xF15)
  //   misa (0x301)
  //   mstatush (0x310)
  //   marchid (0xF12)
  //   mimpid (0xF13)
  //   mhartid (0xF14)
  //   mstatus (0x300)
endmodule
