// Digital circuit EXE_MEM register.dig as structural Verilog
module EXE_MEM_register (
  input  [31:0] Sum_EXE,
  input  [31:0] RF_B_EXE,
  input  [31:0] upper_imm_EXE,
  input  [31:0] PC_plus_4_EXE,
  input  clock,
  input  [1:0] RF_mux_EXE,
  input  RAM_w_EXE,
  input  [2:0] Fct3_EXE,
  input  RF_w_EXE,
  input  [4:0] RF_w_addr_EXE,
  input  enable,
  input  reset,
  output [31:0] Sum_MEM,
  output [31:0] RF_B_MEM,
  output [31:0] upper_imm_MEM,
  output [31:0] PC_plus_4_MEM,
  output [1:0] RF_mux_MEM,
  output RAM_w_MEM,
  output [2:0] Fct3_MEM,
  output RF_w_MEM,
  output [4:0] RF_w_addr_MEM
);

  wire and_1_out, and_2_out, or_1_out, register_1_q, register_3_q;
  wire [4:0] and_3_out, register_5_q;
  wire [4:4] not_1_out, not_2_out;

  and and_1 (and_1_out, RAM_w_EXE, not_1_out[4]);
  and and_2 (and_2_out, RF_w_EXE, not_1_out[4]);
  assign and_3_out = RF_w_addr_EXE & {5{not_1_out[4]}};  // And and_3, 5 bits wide
  not not_1 (not_1_out[4], reset);
  Register register_1 (.D(and_1_out), .C(clock), .en(or_1_out), .Q(register_1_q));
  Register #(.Bits(2)) register_2 (.D(RF_mux_EXE), .C(clock), .en(or_1_out), .Q(RF_mux_MEM));
  Register register_3 (.D(and_2_out), .C(clock), .en(or_1_out), .Q(register_3_q));
  Register #(.Bits(3)) register_4 (.D(Fct3_EXE), .C(clock), .en(or_1_out), .Q(Fct3_MEM));
  Register #(.Bits(5)) register_5 (.D(and_3_out), .C(clock), .en(or_1_out), .Q(register_5_q));
  Register #(.Bits(32)) register_6 (.D(Sum_EXE), .C(clock), .en(or_1_out), .Q(Sum_MEM));
  Register #(.Bits(32)) register_7 (.D(RF_B_EXE), .C(clock), .en(or_1_out), .Q(RF_B_MEM));
  Register #(.Bits(32)) register_8 (.D(upper_imm_EXE), .C(clock), .en(or_1_out), .Q(upper_imm_MEM));
  Register #(.Bits(32)) register_9 (.D(PC_plus_4_EXE), .C(clock), .en(or_1_out), .Q(PC_plus_4_MEM));
  or or_1 (or_1_out, enable, reset);
  and and_4 (RAM_w_MEM, register_1_q, not_2_out[4]);
  and and_5 (RF_w_MEM, register_3_q, not_2_out[4]);
  assign RF_w_addr_MEM = register_5_q & {5{not_2_out[4]}};  // And and_6, 5 bits wide
  not not_2 (not_2_out[4], reset);
endmodule
