// Digital circuit ID_EXE register.dig as structural Verilog
module ID_EXE_register (
  input  [31:0] A_op_ID,
  input  [31:0] B_op_ID,
  input  [31:0] RF_B_ID,
  input  [31:0] upper_imm_ID,
  input  [31:0] PC_ID,
  input  clock,
  input  enable,
  input  [1:0] RF_mux_ID,
  input  RAM_w_ID,
  input  ALU_mux_ID,
  input  [2:0] Fct3_ID,
  input  _30__ID,
  input  op__ID,
  input  RF_w_ID,
  input  [4:0] RF_w_addr_ID,
  input  stall,
  input  reset,
  input  [1:0] B_mux_ID,
  output [31:0] A_op_EXE,
  output [31:0] B_op_EXE,
  output [31:0] RF_B_EXE,
  output [31:0] upper_imm_EXE,
  output [31:0] PC_EXE,
  output [1:0] RF_mux_EXE,
  output RAM_w_EXE,
  output ALU_mux_EXE,
  output [2:0] Fct3_EXE,
  output _30__EXE,
  output op__EXE,
  output RF_w_EXE,
  output [4:0] RF_w_addr_EXE,
  output [1:0] B_mux_EXE
);

  wire and_2_out, and_3_out, or_1_out, register_1_q, register_3_q;
  wire [4:0] and_1_out, register_9_q;
  wire [4:4] nor_1_out, not_1_out;

  assign and_1_out = RF_w_addr_ID & {5{nor_1_out[4]}};  // And and_1, 5 bits wide
  nor nor_1 (nor_1_out[4], stall, reset);
  and and_2 (and_2_out, RF_w_ID, nor_1_out[4]);
  and and_3 (and_3_out, RAM_w_ID, nor_1_out[4]);
  Register register_1 (.D(and_2_out), .C(clock), .en(or_1_out), .Q(register_1_q));
  Register #(.Bits(2)) register_2 (.D(RF_mux_ID), .C(clock), .en(or_1_out), .Q(RF_mux_EXE));
  Register register_3 (.D(and_3_out), .C(clock), .en(or_1_out), .Q(register_3_q));
  Register register_4 (.D(ALU_mux_ID), .C(clock), .en(or_1_out), .Q(ALU_mux_EXE));
  Register #(.Bits(3)) register_5 (.D(Fct3_ID), .C(clock), .en(or_1_out), .Q(Fct3_EXE));
  Register register_6 (.D(_30__ID), .C(clock), .en(or_1_out), .Q(_30__EXE));
  Register register_7 (.D(op__ID), .C(clock), .en(or_1_out), .Q(op__EXE));
  Register #(.Bits(2)) register_8 (.D(B_mux_ID), .C(clock), .en(or_1_out), .Q(B_mux_EXE));
  Register #(.Bits(5)) register_9 (.D(and_1_out), .C(clock), .en(or_1_out), .Q(register_9_q));
  Register #(.Bits(32)) register_10 (.D(A_op_ID), .C(clock), .en(or_1_out), .Q(A_op_EXE));
  Register #(.Bits(32)) register_11 (.D(B_op_ID), .C(clock), .en(or_1_out), .Q(B_op_EXE));
  Register #(.Bits(32)) register_12 (.D(RF_B_ID), .C(clock), .en(or_1_out), .Q(RF_B_EXE));
  Register #(.Bits(32)) register_13 (.D(upper_imm_ID), .C(clock), .en(or_1_out), .Q(upper_imm_EXE));
  Register #(.Bits(32)) register_14 (.D(PC_ID), .C(clock), .en(or_1_out), .Q(PC_EXE));
  or or_1 (or_1_out, stall, enable, reset);
  not not_1 (not_1_out[4], reset);
  and and_4 (RF_w_EXE, register_1_q, not_1_out[4]);
  and and_5 (RAM_w_EXE, register_3_q, not_1_out[4]);
  assign RF_w_addr_EXE = register_9_q & {5{not_1_out[4]}};  // And and_6, 5 bits wide
  // Pins of 1 and 2 bits meet at B_mux_EXE
endmodule
