// Digital circuit IF_ID register.dig as structural Verilog
module IF_ID_register (
  input  clock,
  input  enable,
  input  [31:0] PC_IF,
  input  [31:0] Instr_IF,
  input  reset,
  output [31:0] PC_ID,
  output [31:0] Instr_ID
);

  wire or_1_out;
  wire [31:0] register_2_q;

  or or_1 (or_1_out, enable, reset);
  Register #(.Bits(32)) register_1 (.D(PC_IF), .C(clock), .en(or_1_out), .Q(PC_ID));
  Register #(.Bits(32)) register_2 (.D(Instr_IF), .C(clock), .en(or_1_out), .Q(register_2_q));
  Multiplexer #(.Bits(32)) multiplexer_1 (.sel(reset), .in_0(register_2_q), .in_1(32'h13), .out(Instr_ID));
endmodule
