// Digital circuit Instructions rom.dig as structural Verilog
module Instructions_rom (
  input  [31:0] addr,
  output [31:0] instr
);

  ROM #(.AddrBits(14), .Bits(32)) Instructions_rom (.A(addr[15:2]), .sel(1'b1), .D(instr));

  // Notes on the sheet:
  //   contents of Instructions_rom (hex, n*v repeats v):
  //   13,13,10500073,21*13
endmodule
