// Digital circuit MEM_WB register.dig as structural Verilog
module MEM_WB_register (
  input  [31:0] Sum_MEM,
  input  [31:0] RAM_MEM,
  input  [31:0] upper_imm_MEM,
  input  [31:0] PC_plus_4_MEM,
  input  clock,
  input  enable,
  input  [1:0] RF_mux_MEM,
  input  RF_w_MEM,
  input  [4:0] RF_w_addr_MEM,
  input  reset,
  output [31:0] Sum_WB,
  output [31:0] RAM_WB,
  output [31:0] upper_imm_WB,
  output [31:0] PC_plus_4_WB,
  output [1:0] RF_mux_WB,
  output RF_w_WB,
  output [4:0] RF_w_addr_WB
);

  wire and_1_out, or_1_out, register_2_q;
  wire [4:0] and_2_out, register_3_q;
  wire [4:4] not_1_out, not_2_out;

  not not_1 (not_1_out[4], reset);
  and and_1 (and_1_out, RF_w_MEM, not_1_out[4]);
  assign and_2_out = RF_w_addr_MEM & {5{not_1_out[4]}};  // And and_2, 5 bits wide
  Register #(.Bits(2)) register_1 (.D(RF_mux_MEM), .C(clock), .en(or_1_out), .Q(RF_mux_WB));
  Register register_2 (.D(and_1_out), .C(clock), .en(or_1_out), .Q(register_2_q));
  Register #(.Bits(5)) register_3 (.D(and_2_out), .C(clock), .en(or_1_out), .Q(register_3_q));
  Register #(.Bits(32)) register_4 (.D(Sum_MEM), .C(clock), .en(or_1_out), .Q(Sum_WB));
  Register #(.Bits(32)) register_5 (.D(RAM_MEM), .C(clock), .en(or_1_out), .Q(RAM_WB));
  Register #(.Bits(32)) register_6 (.D(upper_imm_MEM), .C(clock), .en(or_1_out), .Q(upper_imm_WB));
  Register #(.Bits(32)) register_7 (.D(PC_plus_4_MEM), .C(clock), .en(or_1_out), .Q(PC_plus_4_WB));
  or or_1 (or_1_out, enable, reset);
  and and_3 (RF_w_WB, register_2_q, not_2_out[4]);
  assign RF_w_addr_WB = register_3_q & {5{not_2_out[4]}};  // And and_4, 5 bits wide
  not not_2 (not_2_out[4], reset);
endmodule
