// Digital circuit adder.dig as structural Verilog
module adder (
  input  [31:0] A,
  input  [31:0] B,
  output [31:0] Sum
);

  Add #(.Bits(32)) add_1 (.a(A), .b(B), .c_i(1'b0), .s(Sum));  // open: c_o
endmodule
