// Digital circuit arethmetic and logic unit.dig as structural Verilog
module arethmetic_and_logic_unit (
  input  [31:0] A,
  input  [31:0] B,
  input  [2:0] func,
  input  _30,
  input  op,
  output [31:0] Sum
);

  wire sub;
  wire [0:0] slt_lt, sltu_lt;
  wire [31:0] adder_s, and_1_out, multiplexer_1_out, not_1_out, or_1_out,
       shifter_logic_arithmetic_right_1_out, shifter_logical_left_1_out, xor_1_out;

  assign not_1_out = ~B;  // Not not_1, 32 bits wide
  Multiplexer #(.Bits(32)) multiplexer_1 (.sel(sub), .in_0(B), .in_1(not_1_out), .out(multiplexer_1_out));
  Add #(.Bits(32)) adder (.a(A), .b(multiplexer_1_out), .c_i(sub), .s(adder_s));  // open: c_o
  shifter_logical_left shifter_logical_left_1 (.in(A), .out(shifter_logical_left_1_out), .shmt(B[4:0]));
  Comparator #(.Signed("true"), .Bits(32)) slt (.a(A), .b(B), .lt(slt_lt[0]));  // open: gt, eq
  Comparator #(.Bits(32)) sltu (.a(A), .b(B), .lt(sltu_lt[0]));  // open: gt, eq
  assign xor_1_out = A ^ B;  // XOr xor_1, 32 bits wide
  shifter_logic_arithmetic_right shifter_logic_arithmetic_right_1 (
    .in(A), .out(shifter_logic_arithmetic_right_1_out), .shmt(B[4:0]), .arith(_30));
  assign or_1_out = A | B;  // Or or_1, 32 bits wide
  assign and_1_out = A & B;  // And and_1, 32 bits wide
  Multiplexer #(.Selector_Bits(3), .Bits(32)) multiplexer_2 (
    .sel(func), .in_0(adder_s), .in_1(shifter_logical_left_1_out), .in_2({{31{1'b0}}, slt_lt[0]}),
    .in_3({{31{1'b0}}, sltu_lt[0]}), .in_4(xor_1_out), .in_5(shifter_logic_arithmetic_right_1_out),
    .in_6(or_1_out), .in_7(and_1_out), .out(Sum));
  and and_2 (sub, _30, op);
endmodule
