// Digital circuit brunch comparison.dig as structural Verilog
module brunch_comparison (
  input  [31:0] A,
  input  [31:0] B,
  input  [2:0] func,
  output Bcond
);

  wire not_1_out, not_2_out, not_3_out, slt_eq, slt_lt, sltu_lt;

  Comparator #(.Signed("true"), .Bits(32)) slt (.a(A), .b(B), .eq(slt_eq), .lt(slt_lt));  // open: gt
  Comparator #(.Bits(32)) sltu (.a(A), .b(B), .lt(sltu_lt));  // open: gt, eq
  not not_1 (not_1_out, slt_eq);
  not not_2 (not_2_out, slt_lt);
  not not_3 (not_3_out, sltu_lt);
  Multiplexer #(.Selector_Bits(3)) multiplexer_1 (
    .sel(func), .in_0(slt_eq), .in_1(not_1_out), .in_2(1'b0), .in_3(1'b0), .in_4(slt_lt), .in_5(not_2_out),
    .in_6(sltu_lt), .in_7(not_3_out), .out(Bcond));
endmodule
