// Digital circuit cpu.dig as structural Verilog
module cpu (
  input  clk,
  input  reset
);

  wire _4, _5, _7, _20, _30, _31, A_mux, and_2_out, B_cond, B_mux_EXE, control_unit_1_alu_mux,
       control_unit_1_ram_w, csr_access_fault_exception, ebreak_exception, ecall_exception,
       equality_checker_1_a_eq_b, equality_checker_1_a_eq_c, equality_checker_2_a_eq_b,
       equality_checker_2_a_eq_c, equality_checker_3_a_eq_b, equality_checker_3_a_eq_c, EXE_flush,
       exe_mem_register_1_rf_w_mem, freeze, fwd_mux_rs1, fwd_mux_rs2, id_exe_register_1_p12,
       id_exe_register_1_p13, id_exe_register_1_p15, id_exe_register_1_p19, id_exe_register_1_p20, ID_flush,
       illegale_instruction_exception, instuction_access_fault_exception, instuction_misalinged_exception,
       load_misaligned_exception, mret, no_seq_detect, not_1_out, or_1_out, or_2_out, PC_en, RAM_w, reset_t,
       RF_w, RFw, stall_DECODE, stall_EXE, store_misaligned_exception, SUM_mux, system, trap;
  wire [1:0] B_mux, control_unit_1_rf_mux, mem_wb_register_1_rf_mux_wb, PC_mux, RF_mux_EXE, RF_mux_MEM;
  wire [2:0] csr_funct3, funct3_14_12, funct3_EXE, funct3_MEM, multiplexer_12_out;
  wire [3:0] _11_8;
  wire [4:0] exe_mem_register_1_rf_w_addr_mem, multiplexer_11_out, RF_waddr, undriven;
  wire [6:0] opcode;
  wire [7:3] imm_19_12;
  wire [8:0] _30_21;
  wire [11:0] csr_address;
  wire [31:0] adder_1_sum, adder_2_sum, adder_3_sum, ALU_EXE, ALU_MEM, csr, exe_mem_register_1_rf_b_mem,
       id_exe_register_1_p17, id_exe_register_1_p18, id_exe_register_1_p21, instruction,
       instructions_rom_1_instr, JB_target, large_sign_extender_1__32_bits, mem_wb_register_1_pc_plus_4_wb,
       mem_wb_register_1_ram_wb, mem_wb_register_1_sum_wb, mem_wb_register_1_upper_imm_wb, mepc, mtvec,
       multiplexer_1_out, multiplexer_3_out, multiplexer_4_out, multiplexer_5_out, multiplexer_6_out,
       multiplexer_8_out, multiplexer_9_out, multiplexer_10_out, PC_EXE, PC_ID, PC_IF, PC_plus_4_EXE,
       PC_plus_4_MEM, RAM_MEM, register_file_1_a, register_file_1_b, RF_fwd_rs1, RF_fwd_rs2, RF_rs1,
       RF_write_reg_WB, shifter_1_out, Sign_extender_2__32_bits, Sign_extender_3__32_bits,
       Sign_extender__32_bits, trap_manager_1_mcause, trap_manager_1_mepc, trap_manager_1_mtval, UI_EXE,
       UI_MEM;

  // Probe on {adder_3_sum[31:1], 1'b0}
  // Probe on adder_1_sum
  trap_manager trap_manager_1 (
    .Illegal_instruction_exception(illegale_instruction_exception),
    .CSR_access_fault_exception(csr_access_fault_exception), .ebreak_exception(ebreak_exception),
    .ecall_exception(ecall_exception), .load_misaligned_exception(load_misaligned_exception),
    .store_misaligned_exception(store_misaligned_exception),
    .instruction_misaligned_exeption(instuction_misalinged_exception),
    .instruction_access_exception(instuction_access_fault_exception), .decoding_stage_flush(ID_flush),
    .execution_stage_flush(EXE_flush), .trap(trap), .mcause(trap_manager_1_mcause),
    .mepc(trap_manager_1_mepc), .mtval(trap_manager_1_mtval), .PC_IF(PC_IF), .PC_ID(PC_ID), .PC_EXE(PC_EXE),
    .instr(instruction), .Brunch_Jump_target(JB_target), .RAM_address(ALU_EXE));
  // Probe on PC_EXE
  // Probe on PC_ID
  // Probe on PC_IF
  Multiplexer #(.Bits(32)) multiplexer_1 (
    .sel(B_cond), .in_0(adder_1_sum), .in_1(adder_2_sum), .out(multiplexer_1_out));
  initial_state initial_state_1 (.rst(reset), .reset(reset_t), .clk(clk));
  // Probe on JB_target
  // Probe on PC_mux
  Multiplexer #(.Selector_Bits(2), .Bits(32)) multiplexer_2 (
    .sel(PC_mux), .in_0({adder_3_sum[31:1], 1'b0}), .in_1(adder_2_sum), .in_2(adder_1_sum),
    .in_3(multiplexer_1_out), .out(JB_target));
  // Probe on mtvec
  // Probe on trap_manager_1_mepc
  // Probe on ALU_EXE
  // Probe on JB_target
  // Probe on instruction
  // Probe on mepc
  Multiplexer #(.Selector_Bits(2), .Bits(32)) multiplexer_3 (
    .sel({trap, mret}), .in_0(JB_target), .in_1(mepc), .in_2(mtvec), .in_3(mtvec), .out(multiplexer_3_out));
  // Probe on multiplexer_3_out
  adder adder_1 (.A(multiplexer_5_out), .B(32'h4), .Sum(adder_1_sum));
  // Probe on trap_manager_1_mcause
  // Probe on trap_manager_1_mtval
  // Probe on csr_funct3
  // Probe on imm_19_12
  // no_sequenial_execution_detection no_sequenial_execution_detection_1: pin names not known; wires that end beside it: B_cond, {opcode[6], _5, _4, opcode[3:0]}, trap, mret, no_seq_detect
  Multiplexer #(.Bits(32)) multiplexer_4 (
    .sel(no_seq_detect), .in_0(multiplexer_3_out), .in_1(adder_1_sum), .out(multiplexer_4_out));
  Multiplexer #(.Bits(32)) multiplexer_5 (
    .sel(no_seq_detect), .in_0(PC_IF), .in_1(multiplexer_3_out), .out(multiplexer_5_out));
  // Probe on PC_IF
  zicsr_extension zicsr_extension_1 (
    .funct3(csr_funct3), .csr_address(csr_address), .mcause(trap_manager_1_mcause),
    .mepc(trap_manager_1_mepc), .mtval(trap_manager_1_mtval), .RF_to_CSR(RF_rs1), .rs1(imm_19_12),
    .clock(clk), .rst(reset_t), .system(system), .trap(trap), .stall(or_1_out), .freeze_pipeline(freeze),
    .istruction_access_fault_exception(csr_access_fault_exception), .ebreak_exception(ebreak_exception),
    .ecall_exception(ecall_exception), .mret(mret), .mepc_out(mepc), .mtvec(mtvec), .CSR_to_RF(csr));
  // Probe on csr_address
  // Probe on RF_rs1
  instructions_exceptions_detector instructions_exceptions_detector_1 (
    .non_sequential_instr(no_seq_detect), .PC_input(JB_target), .PC_output(PC_IF),
    .Instruction_Address_misaligned(instuction_misalinged_exception),
    .instruction_access_fault(instuction_access_fault_exception));
  program_counter program_counter_1 (
    .instr_addr(PC_IF), .clock(clk), .reset(reset_t), .new_addr(multiplexer_4_out), .enable(PC_en));
  // Probe on multiplexer_4_out
  Instructions_rom instructions_rom_1 (.instr(instructions_rom_1_instr), .addr(multiplexer_5_out));
  // Probe on multiplexer_5_out
  or or_1 (or_1_out, EXE_flush, stall_EXE);
  // Probe on mepc
  // Probe on mtvec
  // Probe on csr
  IF_ID_register if_id_register_1 (
    .clock(clk), .enable(PC_en), .PC_ID(PC_ID), .Instr_ID(instruction), .PC_IF(multiplexer_5_out),
    .Instr_IF(instructions_rom_1_instr), .reset(reset_t));
  // Probe on instructions_rom_1_instr
  // Probe on multiplexer_5_out
  and and_1 (PC_en, freeze, stall_DECODE);
  system_instructions_predecoder system_instructions_predecoder_1 (
    .ID_flush(ID_flush), .instruction(instruction),
    .new_instruction({_31, _30, _30_21, _20, imm_19_12, funct3_14_12, _11_8, _7, opcode[6], _5, _4, opcode[3:0]}),
    .csr_address(csr_address), .csr_funct3(csr_funct3), .illegal_instruction(illegale_instruction_exception),
    .system(system));
  // Probe on instruction
  // Probe on csr_address
  // Probe on csr_funct3
  // Probe on adder_2_sum
  control_unit control_unit_1 (
    .PC_mux(PC_mux), .RF_w(RFw), .A_mux(A_mux), .B_mux(B_mux), .ALU_mux(control_unit_1_alu_mux),
    .RAM_w(control_unit_1_ram_w), .RF_mux(control_unit_1_rf_mux), .SUM_mux(SUM_mux),
    .instr({opcode[6], _5, _4, opcode[3:2]}));
  // Probe on {opcode[6], _5, _4, opcode[3:0]}
  // Probe on {_31, _30, _30_21, _20, imm_19_12, funct3_14_12, _11_8, _7, opcode[6], _5, _4, opcode[3:0]}
  adder adder_2 (.A(multiplexer_6_out), .B(PC_ID), .Sum(adder_2_sum));
  // Probe on control_unit_1_rf_mux
  // Probe on RF_write_reg_WB
  // Probe on {Sign_extender_3__32_bits[30:0], 1'b0}
  Multiplexer #(.Bits(32)) multiplexer_6 (
    .sel(SUM_mux), .in_0({large_sign_extender_1__32_bits[30:0], 1'b0}),
    .in_1({Sign_extender_3__32_bits[30:0], 1'b0}), .out(multiplexer_6_out));
  // Probe on {large_sign_extender_1__32_bits[30:0], 1'b0}
  // Probe on imm_19_12
  // Probe on {_30_21[3:0], _20}
  registers_forwarding registers_forwarding_1 (
    .A_eq_B_EXE(equality_checker_1_a_eq_b), .A_eq_C_EXE(equality_checker_1_a_eq_c),
    .A_eq_B_MEM(equality_checker_2_a_eq_b), .A_eq_C_MEM(equality_checker_2_a_eq_c),
    .A_eq_B_WB(equality_checker_3_a_eq_b), .A_eq_C_WB(equality_checker_3_a_eq_c), .UI_EXE(UI_EXE),
    .ALU_EXE(ALU_EXE), .PC_plus_4_EXE(PC_plus_4_EXE), .RF_mux_EXE(RF_mux_EXE), .UI_MEM(UI_MEM),
    .ALU_MEM(ALU_MEM), .RAM_MEM(RAM_MEM), .RF_mux_MEM(RF_mux_MEM), .PC_plus_4_MEM(PC_plus_4_MEM),
    .Stall_EXE(stall_EXE), .Stall_DECODE(stall_DECODE), .fwd_mux_rs1(fwd_mux_rs1), .RF_fwd_rs1(RF_fwd_rs1),
    .fwd_mux_rs2(fwd_mux_rs2), .RF_fwd_rs2(RF_fwd_rs2), .RF_write_reg_WB(RF_write_reg_WB));
  brunch_comparison brunch_comparison_1 (.A(RF_rs1), .B(multiplexer_8_out), .func(funct3_14_12), .Bcond(B_cond));
  not not_1 (not_1_out, clk);
  register_file register_file_1 (
    .clock(not_1_out), .write(RF_w), .A(register_file_1_a), .B(register_file_1_b), .A_addr(imm_19_12),
    .B_addr({_30_21[3:0], _20}), .wr_addr(RF_waddr), .write_reg(RF_write_reg_WB));
  // Probe on RF_waddr
  sign_extender Sign_extender (._12_bits({_31, _30, _30_21, _20}), ._32_bits(Sign_extender__32_bits));
  sign_extender Sign_extender_2 (._12_bits({_31, _30, _30_21[8:4], _11_8, _7}), ._32_bits(Sign_extender_2__32_bits));
  shifter shifter_1 (.in({_31, _30, _30_21, _20, imm_19_12, funct3_14_12}), .out(shifter_1_out));
  sign_extender Sign_extender_3 (._12_bits({_31, _7, _30, _30_21[8:4], _11_8}), ._32_bits(Sign_extender_3__32_bits));
  large_sign_extender large_sign_extender_1 (
    ._20_bits({_31, imm_19_12, funct3_14_12, _20, _30, _30_21}), ._32_bits(large_sign_extender_1__32_bits));
  // Probe on register_file_1_a
  Multiplexer #(.Bits(32)) multiplexer_7 (.sel(fwd_mux_rs1), .in_0(register_file_1_a), .in_1(RF_fwd_rs1), .out(RF_rs1));
  Multiplexer #(.Bits(32)) multiplexer_8 (
    .sel(fwd_mux_rs2), .in_0(register_file_1_b), .in_1(RF_fwd_rs2), .out(multiplexer_8_out));
  // Probe on register_file_1_b
  // Probe on PC_ID
  adder adder_3 (.A(RF_rs1), .B(Sign_extender__32_bits), .Sum(adder_3_sum));
  // Probe on RF_rs1
  // Probe on multiplexer_8_out
  // Probe on csr
  // Probe on Sign_extender__32_bits
  Multiplexer #(.Selector_Bits(2), .Bits(32)) multiplexer_9 (
    .sel({system, A_mux}), .in_0(PC_ID), .in_1(RF_rs1), .in_2(csr), .in_3(csr), .out(multiplexer_9_out));
  Multiplexer #(.Selector_Bits(2), .Bits(32)) multiplexer_10 (
    .sel(B_mux), .in_0(multiplexer_8_out), .in_1(Sign_extender__32_bits), .in_2(Sign_extender_2__32_bits),
    .in_3(shifter_1_out), .out(multiplexer_10_out));
  // Probe on Sign_extender_2__32_bits
  // Probe on shifter_1_out
  // Probe on funct3_14_12
  // Probe on multiplexer_9_out
  // Probe on multiplexer_10_out
  // Probe on B_mux
  // Probe on multiplexer_8_out
  and and_2 (and_2_out, _5, _4);
  // Probe on B_mux
  Multiplexer #(.Bits(5)) multiplexer_11 (.sel(RFw), .in_0({5{1'b0}}), .in_1({_11_8, _7}), .out(multiplexer_11_out));
  // Probe on multiplexer_11_out
  or or_2 (or_2_out, reset_t, EXE_flush);
  // ID_EXE_register id_exe_register_1: pin names not known; wires that end beside it: control_unit_1_ram_w, RFw, control_unit_1_rf_mux, control_unit_1_alu_mux, funct3_14_12, multiplexer_9_out, multiplexer_10_out, _30, and_2_out, multiplexer_8_out, clk, id_exe_register_1_p12, id_exe_register_1_p13, RF_mux_EXE, id_exe_register_1_p15, funct3_EXE, id_exe_register_1_p17, id_exe_register_1_p18, id_exe_register_1_p19, id_exe_register_1_p20, id_exe_register_1_p21
  // Probe on RF_mux_EXE
  // Probe on funct3_EXE
  // Probe on id_exe_register_1_p17
  // Probe on id_exe_register_1_p21
  // Probe on B_mux_EXE
  // Probe on multiplexer_12_out
  Multiplexer #(.Bits(3)) multiplexer_12 (
    .sel(id_exe_register_1_p15), .in_0(funct3_EXE), .in_1(3'b000), .out(multiplexer_12_out));
  arethmetic_and_logic_unit arethmetic_and_logic_unit_1 (
    .A(id_exe_register_1_p17), .B(id_exe_register_1_p18), .func(multiplexer_12_out),
    ._30(id_exe_register_1_p19), .Sum(ALU_EXE), .op(id_exe_register_1_p20));
  // Probe on id_exe_register_1_p18
  adder adder_4 (.A(32'h4), .B(PC_EXE), .Sum(PC_plus_4_EXE));
  // Probe on PC_EXE
  equality_checker equality_checker_1 (
    .A(undriven), .B(imm_19_12), .C({_30_21[3:0], _20}), .A_eq_B(equality_checker_1_a_eq_b),
    .A_eq_C(equality_checker_1_a_eq_c));
  EXE_MEM_register exe_mem_register_1 (
    .Sum_EXE(ALU_EXE), .RF_B_EXE(id_exe_register_1_p21), .upper_imm_EXE(UI_EXE),
    .PC_plus_4_EXE(PC_plus_4_EXE), .Sum_MEM(ALU_MEM), .RF_B_MEM(exe_mem_register_1_rf_b_mem),
    .upper_imm_MEM(UI_MEM), .PC_plus_4_MEM(PC_plus_4_MEM), .clock(clk), .RF_mux_MEM(RF_mux_MEM),
    .RAM_w_MEM(RAM_w), .RF_mux_EXE(RF_mux_EXE), .RAM_w_EXE(id_exe_register_1_p12), .Fct3_MEM(funct3_MEM),
    .Fct3_EXE(funct3_EXE), .RF_w_MEM(exe_mem_register_1_rf_w_mem), .RF_w_EXE(id_exe_register_1_p13),
    .RF_w_addr_MEM(exe_mem_register_1_rf_w_addr_mem), .RF_w_addr_EXE(undriven), .enable(freeze),
    .reset(reset_t));
  // Probe on funct3_EXE
  // Probe on ALU_EXE
  // Probe on UI_EXE
  // Probe on PC_plus_4_EXE
  // Probe on undriven
  // Probe on RF_mux_MEM
  // Probe on funct3_MEM
  // Probe on ALU_MEM
  data_ram data_ram_1 (
    .data_out(RAM_MEM), .clock(clk), .func(funct3_MEM), .write(RAM_w), .address(ALU_MEM),
    .data_in(exe_mem_register_1_rf_b_mem));
  // Probe on exe_mem_register_1_rf_b_mem
  // Probe on funct3_EXE
  // misaligned_memory_detector misaligned_memory_detector_1: pin names not known; wires that end beside it: ALU_EXE, funct3_EXE, RF_mux_EXE, B_mux_EXE, load_misaligned_exception, store_misaligned_exception
  // Probe on ALU_EXE
  // Probe on RF_mux_EXE
  equality_checker equality_checker_2 (
    .A(exe_mem_register_1_rf_w_addr_mem), .B(imm_19_12), .C({_30_21[3:0], _20}),
    .A_eq_B(equality_checker_2_a_eq_b), .A_eq_C(equality_checker_2_a_eq_c));
  // Probe on B_mux_EXE
  // Probe on RAM_MEM
  // Probe on UI_MEM
  // Probe on PC_plus_4_MEM
  // Probe on exe_mem_register_1_rf_w_addr_mem
  MEM_WB_register mem_wb_register_1 (
    .Sum_MEM(ALU_MEM), .RAM_MEM(RAM_MEM), .upper_imm_MEM(UI_MEM), .PC_plus_4_MEM(PC_plus_4_MEM),
    .Sum_WB(mem_wb_register_1_sum_wb), .RAM_WB(mem_wb_register_1_ram_wb),
    .upper_imm_WB(mem_wb_register_1_upper_imm_wb), .PC_plus_4_WB(mem_wb_register_1_pc_plus_4_wb),
    .clock(clk), .enable(freeze), .RF_mux_WB(mem_wb_register_1_rf_mux_wb), .RF_mux_MEM(RF_mux_MEM),
    .RF_w_WB(RF_w), .RF_w_MEM(exe_mem_register_1_rf_w_mem), .RF_w_addr_WB(RF_waddr),
    .RF_w_addr_MEM(exe_mem_register_1_rf_w_addr_mem), .reset(reset_t));
  // Probe on mem_wb_register_1_rf_mux_wb
  // Probe on mem_wb_register_1_sum_wb
  // Probe on mem_wb_register_1_ram_wb
  // Probe on mem_wb_register_1_upper_imm_wb
  // Probe on mem_wb_register_1_pc_plus_4_wb
  // Probe on RF_waddr
  Multiplexer #(.Selector_Bits(2), .Bits(32)) multiplexer_13 (
    .sel(mem_wb_register_1_rf_mux_wb), .in_0(mem_wb_register_1_upper_imm_wb),
    .in_1(mem_wb_register_1_sum_wb), .in_2(mem_wb_register_1_ram_wb), .in_3(mem_wb_register_1_pc_plus_4_wb),
    .out(RF_write_reg_WB));
  equality_checker equality_checker_3 (
    .A(RF_waddr), .B(imm_19_12), .C({_30_21[3:0], _20}), .A_eq_B(equality_checker_3_a_eq_b),
    .A_eq_C(equality_checker_3_a_eq_c));

  // Other names for the same wires on the sheet: opcode[5:4] = {_5, _4}; rd_11_7[4:0] = {_11_8, _7};
  //   imm_19_12[2:0] = funct3_14_12; imm_31_12[19:0] = {_31, _30, _30_21, _20, imm_19_12, funct3_14_12};
  //   rs1_19_15[4:0] = imm_19_12; imm_31_20[11:0] = {_31, _30, _30_21, _20}; rs2_24_20[4:0] = {_30_21[3:0], _20};
  //   _30_25[5:0] = {_30, _30_21[8:4]}; imm_31_25[6:0] = {_31, _30, _30_21[8:4]}; _30_21[9] = _30; clock = clk

  // Notes on the sheet:
  //   clk: Hz: 50000
  //   Trap
  //   manager
  //   Init
  //   state
  //   +
  //   no-seq
  //   detection
  //   ROM
  //   Zicsr
  //   extension
  //   instructions
  //   exceptions
  //   detector
  //   PC
  //   IF/ID
  //   system instr
  //   predecoder
  //   CU
  //   jalr
  //   upper imm
  //   branch
  //   B cond
  //   RF
  //   sign ext
  //   imm
  //   store
  //   shifter
  //   jal
  //   RF
  //   write
  //   only
  //   ID/EXE
  //   Forwarding
  //   ALU
  //   =
  //   EXE/MEM
  //   RAM
  //   misaligned
  //   memory
  //   detector
  //   MEM/WB
endmodule
