// Digital circuit csrs addresses arbiter.dig as structural Verilog
module csrs_addresses_arbiter (
  input  [11:0] csr_address,
  output [3:0] mux_selector,
  output illegal_op_detected
);

  wire and_1_out, and_2_out, and_3_out, and_4_out, and_5_out, and_6_out, and_7_out, and_8_out, and_9_out,
       and_10_out, and_11_out, and_12_out, and_13_out, and_14_out, and_15_out, and_16_out, and_17_out,
       and_18_out, and_19_out, and_20_out, or_1_out, or_2_out;
  wire [3:0] and_24_out, and_25_out, and_26_out, and_27_out;
  wire [3:3] and_21_out, and_22_out, and_23_out, or_3_out;

  and and_1 (and_1_out, csr_address[8], csr_address[9], ~csr_address[10], ~csr_address[11]);  // And
  and and_2 (and_2_out, ~csr_address[7], csr_address[6], ~csr_address[5], ~csr_address[4]);  // And
  and and_3 (and_3_out, ~csr_address[7], ~csr_address[6], ~csr_address[5], ~csr_address[4]);  // And
  and and_4 (and_4_out, ~csr_address[6], ~csr_address[5], ~csr_address[4], ~csr_address[3], ~csr_address[2]);  // And
  and and_5 (and_5_out, csr_address[8], csr_address[9], ~csr_address[10], csr_address[11]);  // And
  and and_6 (and_6_out, ~csr_address[3], ~csr_address[2], csr_address[1]);  // And
  and and_7 (and_7_out, ~csr_address[3], csr_address[2], ~csr_address[1]);  // And
  and and_8 (and_8_out, ~csr_address[3], ~csr_address[1], csr_address[0]);  // And
  and and_9 (and_9_out, csr_address[4], ~csr_address[5], ~csr_address[6], ~csr_address[7]);  // And
  and and_10 (and_10_out, csr_address[8], csr_address[9], csr_address[10], csr_address[11]);
  and and_11 (and_11_out, ~csr_address[3], ~csr_address[2], ~csr_address[1], ~csr_address[0]);  // And
  and and_12 (and_12_out, ~csr_address[7], ~csr_address[6], ~csr_address[5], csr_address[4]);  // And
  and and_13 (and_13_out, ~csr_address[3], ~csr_address[2]);  // And
  and and_14 (and_14_out, ~csr_address[3], ~csr_address[1], ~csr_address[0]);  // And
  or or_1 (or_1_out, and_6_out, and_7_out, and_8_out);
  or or_2 (or_2_out, and_13_out, and_14_out);
  and and_15 (and_15_out, and_2_out, and_1_out);
  and and_16 (and_16_out, and_1_out, and_3_out);
  and and_17 (and_17_out, ~csr_address[1], ~csr_address[3]);  // And
  and and_18 (and_18_out, and_4_out, ~csr_address[0]);  // And
  and and_19 (and_19_out, or_1_out, and_9_out, and_10_out);
  and and_20 (and_20_out, and_11_out, and_12_out, and_1_out);
  and and_21 (and_21_out[3], or_2_out, and_15_out);
  and and_22 (and_22_out[3], and_16_out, and_17_out);
  and and_23 (and_23_out[3], and_18_out, and_5_out);
  or or_3 (or_3_out[3], and_19_out, and_20_out);
  assign and_24_out = {4{or_3_out[3]}} & 4'b0111;  // And and_24, 4 bits wide
  assign and_25_out = {4{and_21_out[3]}} & csr_address[3:0];  // And and_25, 4 bits wide
  assign and_26_out = {4{and_22_out[3]}} & {2'b11, csr_address[2], csr_address[0]};  // And and_26, 4 bits wide
  assign and_27_out = {2'b10, csr_address[1], csr_address[7]} & {4{and_23_out[3]}};  // And and_27, 4 bits wide
  nor nor_1 (illegal_op_detected, or_3_out[3], and_21_out[3], and_22_out[3], and_23_out[3]);
  assign mux_selector = and_24_out | and_25_out | and_26_out | and_27_out;  // Or or_4, 4 bits wide

  // Notes on the sheet:
  //   0x3--
  //   0xB--
  //   0x34-
  //   0x30-
  //   0xF1-
  //   0x310
  //   5 6 7
  //   0 1 2 3 4
  //   12 13 14 15
  //   8 9 10 11
endmodule
