// Digital circuit data ram.dig as structural Verilog
module data_ram (
  input  clock,
  input  write,
  input  [31:0] address,
  input  [31:0] data_in,
  input  [2:0] func,
  output [31:0] data_out
);

  wire not_1_out;
  wire [1:1] nor_1_out;

  nor nor_1 (nor_1_out[1], func[0], func[1]);
  not not_1 (not_1_out, func[2]);
  // RAM32Bit #(.generic("addrBits := 16;")) ram32bit_1: pin names not known; wires that end beside it: address[15:0], data_in, write, {nor_1_out[1], func[0]}, not_1_out, clock, data_out
endmodule
