// Digital circuit equality checker.dig as structural Verilog
module equality_checker (
  input  [4:0] A,
  input  [4:0] B,
  input  [4:0] C,
  output A_eq_B,
  output A_eq_C
);

  wire comparator_1_eq, comparator_2_eq, or_1_out;

  Comparator #(.Bits(5)) comparator_1 (.a(A), .b(B), .eq(comparator_1_eq));  // open: gt, lt
  Comparator #(.Bits(5)) comparator_2 (.a(A), .b(C), .eq(comparator_2_eq));  // open: gt, lt
  or or_1 (or_1_out, A[4], A[3], A[2], A[1], A[0]);
  and and_1 (A_eq_B, or_1_out, comparator_1_eq);
  and and_2 (A_eq_C, or_1_out, comparator_2_eq);
endmodule
