// Digital circuit illegal instructions detector.dig as structural Verilog
module illegal_instructions_detector (
  input  [6:0] opcode,
  output illegal_op
);

  wire and_1_out, and_2_out, and_3_out, and_4_out, and_5_out, and_6_out, nand_1_out, nor_1_out, not_1_out,
       not_2_out, not_3_out, not_4_out, not_5_out, or_1_out;

  not not_1 (not_1_out, opcode[2]);
  not not_2 (not_2_out, opcode[3]);
  not not_3 (not_3_out, opcode[4]);
  not not_4 (not_4_out, opcode[5]);
  not not_5 (not_5_out, opcode[6]);
  and and_1 (and_1_out, not_2_out, opcode[4], not_5_out);
  and and_2 (and_2_out, opcode[2], opcode[3], not_3_out, not_4_out, not_5_out);
  and and_3 (and_3_out, not_1_out, not_2_out, not_3_out, not_5_out);
  and and_4 (and_4_out, not_2_out, not_3_out, opcode[5], opcode[6]);
  and and_5 (and_5_out, opcode[2], opcode[3], not_3_out, opcode[5], opcode[6]);
  and and_6 (and_6_out, not_1_out, not_2_out, opcode[4], opcode[5], opcode[6]);
  or or_1 (or_1_out, and_5_out, and_6_out);
  nand nand_1 (nand_1_out, opcode[0], opcode[1]);
  nor nor_1 (nor_1_out, and_1_out, and_2_out, and_3_out, and_4_out, or_1_out);
  or or_2 (illegal_op, nand_1_out, nor_1_out);

  // Notes on the sheet:
  //   OP OP-imm AUIPC LUI
  //   MISC-mem
  //   LOAD STORE
  //   Branch JALR
  //   JAL
  //   SYSTEM
endmodule

/* Test case:
opcode   illegal-op

0         0
1         1
2         1
3         0
4         0
5         0
6         1
7         1
8         0
9         1
10        1
11        1
12        0
13        0
14        1
15        1
16        1
17        1
18        1
19        1
20        1
21        1
22        1
23        1
24        0
25        0
26        1
27        0
28        0
29        1
30        1
31        1
*/
