// Digital circuit initial state.dig as structural Verilog
module initial_state (
  input  rst,
  input  clk,
  output reset
);

  wire d_ff_1_nq, reset_1_out;

  Reset #(.invertOutput("false")) reset_1 (.out(reset_1_out));
  D_FF d_ff_1 (.D(1'b1), .C(clk), .nQ(d_ff_1_nq));  // open: Q
  or or_1 (reset, d_ff_1_nq, reset_1_out, rst);
endmodule
