// Digital circuit instructions counter.dig as structural Verilog
module instructions_counter (
  input  stall,
  input  clock,
  input  reset,
  output count
);

  wire and_1_out, and_2_out, and_3_out, d_ff_1_q, d_ff_2_q, d_ff_3_q, not_1_out, not_2_out;

  not not_1 (not_1_out, stall);
  D_FF d_ff_1 (.D(1'b1), .C(clock), .Q(d_ff_1_q));  // open: nQ
  not not_2 (not_2_out, reset);
  and and_1 (and_1_out, not_2_out, not_1_out, d_ff_1_q);
  D_FF d_ff_2 (.D(and_1_out), .C(clock), .Q(d_ff_2_q));  // open: nQ
  and and_2 (and_2_out, not_2_out, d_ff_2_q);
  D_FF d_ff_3 (.D(and_2_out), .C(clock), .Q(d_ff_3_q));  // open: nQ
  and and_3 (and_3_out, not_2_out, d_ff_3_q);
  D_FF d_ff_4 (.D(and_3_out), .C(clock), .Q(count));  // open: nQ
endmodule
