// Digital circuit instructions exceptions detector.dig as structural Verilog
module instructions_exceptions_detector (
  input  non_sequential_instr,
  input  [31:0] PC_input,
  input  [31:0] PC_output,
  output Instruction_Address_misaligned,
  output instruction_access_fault
);

  wire or_1_out;

  or or_1 (or_1_out, PC_input[0], PC_input[1]);
  or or_2 (instruction_access_fault, PC_output[0], PC_output[1]);
  and and_1 (Instruction_Address_misaligned, non_sequential_instr, or_1_out);
endmodule
