// Digital circuit large sign extender.dig as structural Verilog
module large_sign_extender (
  input  [19:0] _20_bits,
  output [31:0] _32_bits
);

  BitExtender #(.inputBits(20), .outputBits(32)) Sign_Extend (.in(_20_bits), .out(_32_bits));
endmodule
