// Digital circuit misaligned memory detector.dig as structural Verilog
module misaligned_memory_detector (
  input  [31:0] RAM_address,
  input  [1:0] B_mux,
  input  [1:0] RF_mux,
  input  [2:0] Funct3,
  output Load_Address_Misaligned,
  output Store_Address_Misaligned
);

  wire and_1_out, and_2_out, and_3_out, and_4_out, and_5_out, and_6_out, and_7_out, and_8_out, and_9_out,
       and_10_out, and_11_out, not_1_out, not_2_out, not_3_out, or_1_out;

  or or_1 (or_1_out, RAM_address[0], RAM_address[1]);
  not not_1 (not_1_out, Funct3[2]);
  not not_2 (not_2_out, Funct3[1]);
  not not_3 (not_3_out, Funct3[0]);
  and and_1 (and_1_out, Funct3[0], not_2_out, not_1_out);
  and and_2 (and_2_out, not_3_out, Funct3[1], not_1_out);
  and and_3 (and_3_out, Funct3[0], not_2_out, Funct3[2]);
  and and_4 (and_4_out, RF_mux[1], ~RF_mux[0]);  // And
  and and_5 (and_5_out, B_mux[0], ~B_mux[1], and_4_out);  // And
  and and_6 (and_6_out, ~B_mux[0], B_mux[1], and_4_out);  // And
  and and_7 (and_7_out, and_5_out, and_1_out, RAM_address[0]);
  and and_8 (and_8_out, and_5_out, and_2_out, or_1_out);
  and and_9 (and_9_out, and_5_out, and_3_out, RAM_address[0]);
  and and_10 (and_10_out, and_6_out, and_1_out, RAM_address[0]);
  and and_11 (and_11_out, and_6_out, and_2_out, or_1_out);
  or or_2 (Load_Address_Misaligned, and_7_out, and_8_out, and_9_out);
  or or_3 (Store_Address_Misaligned, and_10_out, and_11_out);

  // Notes on the sheet:
  //   1
  //   2
  //   5
endmodule
