// Digital circuit mstatus regiter.dig as structural Verilog
module mstatus_regiter (
  input  [31:0] \input ,
  input  clock,
  input  write,
  input  trap_firing,
  input  mret,
  output [31:0] \output 
);

  wire and_1_out, multiplexer_1_out, multiplexer_2_out, or_1_out, or_2_out, or_3_out;

  Multiplexer multiplexer_1 (.sel(trap_firing), .in_0(\input [7]), .in_1(\output [3]), .out(multiplexer_1_out));
  Multiplexer multiplexer_2 (.sel(mret), .in_0(\input [3]), .in_1(\output [7]), .out(multiplexer_2_out));
  or or_1 (or_1_out, multiplexer_1_out, mret);
  and and_1 (and_1_out, multiplexer_2_out, ~trap_firing);  // And
  or or_2 (or_2_out, write, mret, trap_firing);
  or or_3 (or_3_out, write, mret, trap_firing);
  Register MPIE__7 (.D(or_1_out), .C(clock), .en(or_2_out), .Q(\output [7]));
  Register MIE__3 (.D(and_1_out), .C(clock), .en(or_3_out), .Q(\output [3]));

  assign {\output [31:8], \output [6:4], \output [2:0]} = {30{1'b0}};

  // Other names for the same wires on the sheet: clk = clock
endmodule
