// Digital circuit no sequenial execution detection.dig as structural Verilog
module no_sequenial_execution_detection (
  input  [6:0] opcode,
  input  Bond,
  input  [6:0] trap,
  input  [6:0] mret,
  output no_seq_detec
);

  wire and_1_out, and_2_out;

  and and_1 (and_1_out, opcode[5], opcode[6], opcode[2]);
  and and_2 (and_2_out, Bond, opcode[5], opcode[6]);
  or or_1 (no_seq_detec, and_1_out, and_2_out, trap[0], mret[0]);
  // Pins of 1 and 7 bits meet at trap
  // Pins of 1 and 7 bits meet at mret
endmodule
