// Digital circuit program counter.dig as structural Verilog
module program_counter (
  input  clock,
  input  reset,
  input  [31:0] new_addr,
  input  enable,
  output [31:0] instr_addr
);

  wire or_1_out;
  wire [31:0] register_1_q;

  or or_1 (or_1_out, enable, reset);
  Register #(.Bits(32)) register_1 (.D(new_addr), .C(clock), .en(or_1_out), .Q(register_1_q));
  Multiplexer #(.Bits(32)) multiplexer_1 (.sel(reset), .in_0(register_1_q), .in_1(32'h80000000), .out(instr_addr));
endmodule
