// Digital circuit ram32bits.dig as structural Verilog
module ram32bits (
  input  [9:0] in_1,
  input  in_2,
  input  [31:0] in_3,
  input  in_5,
  output [31:0] out_4
);

  BlockRAMDualPort #(.AddrBits(10), .Bits(32)) blockramdualport_1 (
    .A(in_1), .Din(in_3), .str(in_2), .C(in_5), .D(out_4));
endmodule
