// Digital circuit register file.dig as structural Verilog
module register_file (
  input  clock,
  input  write,
  input  [4:0] A_addr,
  input  [4:0] B_addr,
  input  [4:0] wr_addr,
  input  [31:0] write_reg,
  output [31:0] A,
  output [31:0] B
);

  wire and_1_out, zero;

  and and_1 (and_1_out, write, zero);
  RegisterFile #(.AddrBits(5), .Bits(32)) register_file (
    .Din(write_reg), .we(and_1_out), .Rw(wr_addr), .C(clock), .Ra(A_addr), .Rb(B_addr), .Da(A), .Db(B));
  or or_1 (zero, wr_addr[0], wr_addr[1], wr_addr[2], wr_addr[3], wr_addr[4]);
endmodule
