// Digital circuit registers forwarding.dig as structural Verilog
module registers_forwarding (
  input  A_eq_B_EXE,
  input  A_eq_C_EXE,
  input  A_eq_B_MEM,
  input  A_eq_C_MEM,
  input  A_eq_B_WB,
  input  A_eq_C_WB,
  input  [31:0] UI_EXE,
  input  [31:0] ALU_EXE,
  input  [31:0] PC_plus_4_EXE,
  input  [1:0] RF_mux_EXE,
  input  [31:0] UI_MEM,
  input  [31:0] ALU_MEM,
  input  [31:0] RAM_MEM,
  input  [1:0] RF_mux_MEM,
  input  [31:0] PC_plus_4_MEM,
  input  [31:0] RF_write_reg_WB,
  output Stall_EXE,
  output Stall_DECODE,
  output fwd_mux_rs1,
  output [31:0] RF_fwd_rs1,
  output fwd_mux_rs2,
  output [31:0] RF_fwd_rs2
);

  wire and_2_out, or_1_out;
  wire [1:0] priorityencoder_1_num, priorityencoder_2_num;
  wire [31:0] multiplexer_3_out, multiplexer_4_out;

  not not_1 (Stall_DECODE, Stall_EXE);
  and and_1 (Stall_EXE, and_2_out, or_1_out);
  or or_1 (or_1_out, A_eq_B_EXE, A_eq_C_EXE);
  and and_2 (and_2_out, ~RF_mux_EXE[0], RF_mux_EXE[1]);  // And
  PriorityEncoder #(.Selector_Bits(2)) priorityencoder_1 (
    .in0(A_eq_C_WB), .in1(A_eq_C_MEM), .in2(A_eq_C_EXE), .in3(1'b0), .num(priorityencoder_1_num),
    .any(fwd_mux_rs2));
  PriorityEncoder #(.Selector_Bits(2)) priorityencoder_2 (
    .in0(A_eq_B_WB), .in1(A_eq_B_MEM), .in2(A_eq_B_EXE), .in3(1'b0), .num(priorityencoder_2_num),
    .any(fwd_mux_rs1));
  Multiplexer #(.Selector_Bits(2), .Bits(32)) multiplexer_1 (
    .sel(priorityencoder_2_num), .in_0(RF_write_reg_WB), .in_1(multiplexer_4_out), .in_2(multiplexer_3_out),
    .in_3({32{1'b0}}), .out(RF_fwd_rs1));
  Multiplexer #(.Selector_Bits(2), .Bits(32)) multiplexer_2 (
    .sel(priorityencoder_1_num), .in_0(RF_write_reg_WB), .in_1(multiplexer_4_out), .in_2(multiplexer_3_out),
    .in_3({32{1'b0}}), .out(RF_fwd_rs2));
  Multiplexer #(.Selector_Bits(2), .Bits(32)) multiplexer_3 (
    .sel(RF_mux_EXE), .in_0(UI_EXE), .in_1(ALU_EXE), .in_2({32{1'b0}}), .in_3(PC_plus_4_EXE),
    .out(multiplexer_3_out));
  Multiplexer #(.Selector_Bits(2), .Bits(32)) multiplexer_4 (
    .sel(RF_mux_MEM), .in_0(UI_MEM), .in_1(ALU_MEM), .in_2(RAM_MEM), .in_3(PC_plus_4_MEM),
    .out(multiplexer_4_out));

  // Other names for the same wires on the sheet: fwd_rs1 = fwd_mux_rs1; fwd_rs2 = fwd_mux_rs2
endmodule
