// Digital circuit shifter logic arithmetic right.dig as structural Verilog
module shifter_logic_arithmetic_right (
  input  [31:0] in,
  input  [4:0] shmt,
  input  arith,
  output [31:0] out
);

  wire and_1_out;
  wire [1:0] multiplexer_1_out_2, multiplexer_4_out;
  wire [3:0] multiplexer_3_out;
  wire [7:0] multiplexer_2_out;
  wire [27:0] multiplexer_3_out_2;
  wire [29:0] multiplexer_4_out_2;
  wire [31:0] multiplexer_2_out_2, multiplexer_5_out;
  wire [31:28] multiplexer_1_out;
  wire [31:30] multiplexer_1_out_3;

  and and_1 (and_1_out, arith, in[31]);
  Multiplexer #(.Bits(16)) multiplexer_1 (
    .sel(and_1_out), .in_0({16{1'b0}}), .in_1({16{1'b1}}),
    .out({multiplexer_1_out_3, multiplexer_1_out_2, multiplexer_1_out, multiplexer_2_out_2[31:24]}));
  Multiplexer #(.Bits(32)) multiplexer_2 (
    .sel(shmt[4]), .in_0(in),
    .in_1({multiplexer_1_out_3, multiplexer_1_out_2, multiplexer_1_out, multiplexer_2_out_2[31:24], in[31:16]}),
    .out({multiplexer_2_out_2[23:0], multiplexer_2_out}));
  Multiplexer #(.Bits(32)) multiplexer_3 (
    .sel(shmt[3]), .in_0({multiplexer_2_out_2[23:0], multiplexer_2_out}), .in_1(multiplexer_2_out_2),
    .out({multiplexer_3_out_2, multiplexer_3_out}));
  Multiplexer #(.Bits(32)) multiplexer_4 (
    .sel(shmt[2]), .in_0({multiplexer_3_out_2, multiplexer_3_out}),
    .in_1({multiplexer_1_out, multiplexer_3_out_2}), .out({multiplexer_4_out_2, multiplexer_4_out}));
  Multiplexer #(.Bits(32)) multiplexer_5 (
    .sel(shmt[1]), .in_0({multiplexer_4_out_2, multiplexer_4_out}),
    .in_1({multiplexer_1_out_2, multiplexer_4_out_2}), .out(multiplexer_5_out));
  Multiplexer #(.Bits(32)) multiplexer_6 (
    .sel(shmt[0]), .in_0(multiplexer_5_out), .in_1({multiplexer_1_out_3[30], multiplexer_5_out[31:1]}),
    .out(out));
endmodule
