// Digital circuit shifter logical left.dig as structural Verilog
module shifter_logical_left (
  input  [31:0] in,
  input  [4:0] shmt,
  output [31:0] out
);

  wire [31:0] multiplexer_1_out, multiplexer_3_out, multiplexer_4_out;
  wire [31:4] multiplexer_2_out;
  wire [31:28] multiplexer_2_out_2;

  Multiplexer #(.Bits(32)) multiplexer_1 (
    .sel(shmt[4]), .in_0(in), .in_1({in[15:0], {16{1'b0}}}), .out(multiplexer_1_out));
  Multiplexer #(.Bits(32)) multiplexer_2 (
    .sel(shmt[3]), .in_0(multiplexer_1_out), .in_1({multiplexer_1_out[23:0], {8{1'b0}}}),
    .out({multiplexer_2_out_2, multiplexer_2_out}));
  Multiplexer #(.Bits(32)) multiplexer_3 (
    .sel(shmt[2]), .in_0({multiplexer_2_out_2, multiplexer_2_out}), .in_1({multiplexer_2_out, 4'b0000}),
    .out(multiplexer_3_out));
  Multiplexer #(.Bits(32)) multiplexer_4 (
    .sel(shmt[1]), .in_0(multiplexer_3_out), .in_1({multiplexer_3_out[29:0], 2'b00}), .out(multiplexer_4_out));
  Multiplexer #(.Bits(32)) multiplexer_5 (
    .sel(shmt[0]), .in_0(multiplexer_4_out), .in_1({multiplexer_4_out[30:0], 1'b0}), .out(out));
endmodule
