// Digital circuit sign extender.dig as structural Verilog
module sign_extender (
  input  [11:0] _12_bits,
  output [31:0] _32_bits
);

  BitExtender #(.inputBits(12), .outputBits(32)) Sign_Extend (.in(_12_bits), .out(_32_bits));
endmodule
