// Digital circuit system instructions predecoder.dig as structural Verilog
module system_instructions_predecoder (
  input  [31:0] instruction,
  input  ID_flush,
  output [31:0] new_instruction,
  output [2:0] csr_funct3,
  output [11:0] csr_address,
  output system,
  output illegal_instruction
);

  wire and_1_out, or_1_out, or_2_out, or_3_out;
  wire [4:0] and_4_out, and_5_out;
  wire [4:4] and_3_out;

  illegal_instructions_detector illegal_instructions_detector_1 (
    .opcode(instruction[6:0]), .illegal_op(illegal_instruction));
  and and_1 (and_1_out, ~instruction[6], ~instruction[5], ~instruction[4], instruction[3], instruction[2]);  // And
  and and_2 (system, instruction[6], instruction[5], instruction[4], ~instruction[3], ~instruction[2]);  // And
  or or_1 (or_1_out, instruction[12], instruction[13], instruction[14]);
  or or_2 (or_2_out, illegal_instruction, ID_flush, and_1_out);
  and and_3 (and_3_out[4], ~or_2_out, or_1_out);  // And
  or or_3 (or_3_out, or_2_out, system);
  assign and_4_out = instruction[11:7] & {5{and_3_out[4]}};  // And and_4, 5 bits wide
  assign and_5_out = instruction[19:15] & {5{and_3_out[4]}};  // And and_5, 5 bits wide
  Multiplexer #(.Bits(32)) multiplexer_1 (
    .sel(or_3_out), .in_0(instruction), .in_1({{12{1'b0}}, and_5_out, 3'b000, and_4_out, 7'b0010011}),
    .out(new_instruction));

  assign csr_address = instruction[31:20];
  assign csr_funct3 = instruction[14:12];

  // Notes on the sheet:
  //   Fence instruction
  //   System instructions
  //   ANDs to
  //   force the
  //   nop instruction
  //   addi instruction
  //   format
endmodule
