// Digital circuit trap manager.dig as structural Verilog
module trap_manager (
  input  Illegal_instruction_exception,
  input  CSR_access_fault_exception,
  input  ebreak_exception,
  input  ecall_exception,
  input  load_misaligned_exception,
  input  store_misaligned_exception,
  input  instruction_misaligned_exeption,
  input  instruction_access_exception,
  input  [31:0] PC_IF,
  input  [31:0] PC_ID,
  input  [31:0] PC_EXE,
  input  [31:0] instr,
  input  [31:0] Brunch_Jump_target,
  input  [31:0] RAM_address,
  output trap,
  output [31:0] mcause,
  output execution_stage_flush,
  output decoding_stage_flush,
  output [31:0] mepc,
  output [31:0] mtval
);

  wire and_3_out, and_4_out, and_5_out, and_6_out, and_7_out, and_8_out, not_1_out, not_2_out, not_3_out,
       or_5_out;
  wire [1:0] priorityencoder_2_num;
  wire [2:0] priorityencoder_1_num;

  PriorityEncoder #(.Selector_Bits(3)) priorityencoder_1 (
    .in0(instruction_access_exception), .in1(Illegal_instruction_exception),
    .in2(CSR_access_fault_exception), .in3(ebreak_exception), .in4(ecall_exception),
    .in5(instruction_misaligned_exeption), .in6(load_misaligned_exception), .in7(store_misaligned_exception),
    .num(priorityencoder_1_num), .any(trap));
  not not_1 (not_1_out, priorityencoder_1_num[2]);
  not not_2 (not_2_out, priorityencoder_1_num[1]);
  not not_3 (not_3_out, priorityencoder_1_num[0]);
  and and_1 (mcause[3], not_3_out, not_2_out, priorityencoder_1_num[2]);
  and and_2 (mcause[2], priorityencoder_1_num[1], priorityencoder_1_num[2]);
  and and_3 (and_3_out, priorityencoder_1_num[0], not_1_out);
  and and_4 (and_4_out, not_3_out, not_2_out, priorityencoder_1_num[2]);
  and and_5 (and_5_out, priorityencoder_1_num[0], priorityencoder_1_num[1]);
  and and_6 (and_6_out, priorityencoder_1_num[1], not_1_out);
  and and_7 (and_7_out, not_3_out, not_2_out);
  and and_8 (and_8_out, priorityencoder_1_num[0], priorityencoder_1_num[1], not_1_out);
  or or_1 (mcause[1], and_3_out, and_4_out, and_5_out, and_6_out);
  or or_2 (mcause[0], and_7_out, and_8_out);
  or or_3 (execution_stage_flush, store_misaligned_exception, load_misaligned_exception);
  or or_4 (decoding_stage_flush, store_misaligned_exception, load_misaligned_exception, Illegal_instruction_exception, CSR_access_fault_exception, ebreak_exception, ecall_exception);
  or or_5 (or_5_out, instruction_misaligned_exeption, decoding_stage_flush);
  Multiplexer #(.Selector_Bits(3), .Bits(32)) multiplexer_1 (
    .sel(priorityencoder_1_num), .in_0(PC_IF), .in_1(instr), .in_2(instr), .in_3({32{1'b0}}),
    .in_4({32{1'b0}}), .in_5(Brunch_Jump_target), .in_6(RAM_address), .in_7(RAM_address), .out(mtval));
  PriorityEncoder #(.Selector_Bits(2)) priorityencoder_2 (
    .in0(1'b0), .in1(instruction_access_exception), .in2(or_5_out), .in3(execution_stage_flush),
    .num(priorityencoder_2_num));  // open: any
  Multiplexer #(.Selector_Bits(2), .Bits(32)) multiplexer_2 (
    .sel(priorityencoder_2_num), .in_0({32{1'b0}}), .in_1(PC_IF), .in_2(PC_ID), .in_3(PC_EXE), .out(mepc));

  assign mcause[31:4] = {28{1'b0}};

  // Other names for the same wires on the sheet: instruction[31:0] = instr; JB_target[31:0] = Brunch_Jump_target
endmodule
