// Digital circuit zicsr extension.dig as structural Verilog
module zicsr_extension (
  input  [2:0] funct3,
  input  system,
  input  rst,
  input  [11:0] csr_address,
  input  [31:0] RF_to_CSR,
  input  [4:0] rs1,
  input  clock,
  input  [31:0] mcause,
  input  [31:0] mepc,
  input  [31:0] mtval,
  input  trap,
  input  stall,
  output freeze_pipeline,
  output [31:0] CSR_to_RF,
  output mret,
  output [31:0] mepc_out,
  output [31:0] mtvec,
  output istruction_access_fault_exception,
  output ebreak_exception,
  output ecall_exception
);

  wire and_2_out, and_3_out, and_4_out, and_5_out, and_6_out, and_7_out, count, counter_1_ovf, jk_ff_1_nq,
       or_1_out, or_2_out, or_4_out, wfi;
  wire [31:0] and_1_out, multiplexer_1_out, multiplexer_2_out, not_1_out, or_3_out;

  instructions_counter instructions_counter_1 (.stall(stall), .clock(clock), .reset(rst), .count(count));
  or or_1 (or_1_out, funct3[0], funct3[1], funct3[2]);
  Multiplexer #(.Bits(32)) multiplexer_1 (
    .sel(funct3[2]), .in_0(RF_to_CSR), .in_1({{27{1'b0}}, rs1}), .out(multiplexer_1_out));
  or or_2 (or_2_out, wfi, rst);
  assign not_1_out = ~multiplexer_1_out;  // Not not_1, 32 bits wide
  Counter #(.Bits(10)) counter_1 (.en(jk_ff_1_nq), .C(clock), .clr(or_2_out), .ovf(counter_1_ovf));  // open: out
  assign or_3_out = multiplexer_1_out | CSR_to_RF;  // Or or_3, 32 bits wide
  assign and_1_out = not_1_out & CSR_to_RF;  // And and_1, 32 bits wide
  or or_4 (or_4_out, rst, counter_1_ovf);
  Multiplexer #(.Selector_Bits(2), .Bits(32)) multiplexer_2 (
    .sel(funct3[1:0]), .in_0({32{1'b0}}), .in_1(multiplexer_1_out), .in_2(or_3_out), .in_3(and_1_out),
    .out(multiplexer_2_out));
  JK_FF jk_ff_1 (.J(or_4_out), .C(clock), .K(wfi), .Q(freeze_pipeline), .nQ(jk_ff_1_nq));
  CSRs csrs_1 (
    .mepc(mepc), .mcause(mcause), .CSR_write(multiplexer_2_out), .CSR_read(CSR_to_RF), .clock(clock),
    .csr_address(csr_address), .write(and_2_out), .mtval(mtval), .instr_cnt(count),
    .illegal_op(istruction_access_fault_exception), .mtvec(mtvec), .trap(trap), .mepc_read(mepc_out),
    .mret(mret));
  and and_2 (and_2_out, system, or_1_out);
  and and_3 (and_3_out, system, ~or_1_out);  // And
  and and_4 (and_4_out, ~csr_address[11], ~csr_address[10], csr_address[9], csr_address[8], ~csr_address[7], ~csr_address[6], ~csr_address[5], ~csr_address[4], ~csr_address[3], ~csr_address[2], csr_address[1], ~csr_address[0]);  // And
  and and_5 (and_5_out, ~csr_address[11], ~csr_address[10], ~csr_address[9], csr_address[8], ~csr_address[7], ~csr_address[6], ~csr_address[5], ~csr_address[4], ~csr_address[3], csr_address[2], ~csr_address[1], csr_address[0]);  // And
  and and_6 (and_6_out, ~csr_address[11], ~csr_address[10], ~csr_address[9], ~csr_address[8], ~csr_address[7], ~csr_address[6], ~csr_address[5], ~csr_address[4], ~csr_address[3], ~csr_address[2], ~csr_address[1], csr_address[0]);  // And
  and and_7 (and_7_out, ~csr_address[11], ~csr_address[10], ~csr_address[9], ~csr_address[8], ~csr_address[7], ~csr_address[6], ~csr_address[5], ~csr_address[4], ~csr_address[3], ~csr_address[2], ~csr_address[1], ~csr_address[0]);  // And
  and and_8 (mret, and_4_out, and_3_out);
  and and_9 (wfi, and_5_out, and_3_out);
  and and_10 (ebreak_exception, and_6_out, and_3_out);
  and and_11 (ecall_exception, and_7_out, and_3_out);

  // Other names for the same wires on the sheet: clk = clock

  // Notes on the sheet:
  //   instructions
  //   counter
  //   CSR
  //   registers
endmodule
